# Fritzing sketch Dimmer (saved by Fritzing 0.9.2b)
breadboards: 1

parts:
  LED1 = LED - 5mm [color="Red (633nm)" package="5 mm [THT]"]
  R1 = Resistor [tolerance=±5% resistance=220 package=THT]
  Bauteil1 = Arduino Uno (Rev3)
  R3 = Resistor [tolerance=±5% resistance=10k package=THT]
  R4 = PHOTOCELL [package=photocell-kit]

nets:
  N1: LED1.cathode, Bauteil1.D11_PWM/MOSI
  N2: LED1.anode, R1.Pin_0
  N3: R1.Pin_1, Bauteil1.GND, R3.Pin_1
  N4: Bauteil1.A0, R3.Pin_0, R4.P$2
  N5: Bauteil1.5V, R4.P$1

// code stored in the sketch: Bsp02_Blink.ino
/* Blink.ino
 *
 * Copyright 2015 Roland Richter
 *
 * This program is free software: you can redistribute it and/or modify
 * it under the terms of the GNU General Public License as published by
 * the Free Software Foundation, either version 3 of the License, or
 * (at your option) any later version.
 *
 * This program is distributed in the hope that it will be useful,
 * but WITHOUT ANY WARRANTY; without even the implied warranty
 * of MERCHANTABILITY or FITNESS FOR A PARTICULAR PURPOSE.
 * See the GNU General Public License for more details.
 *
 * You should have received a copy of the GNU General Public License
 * along with this program. If not, see <http://www.gnu.org/licenses/>.
 */

#include <Metro.h>

// Der Ausgangs-Pin der LED
const int LEDPin = 7;

// Der momentane Status der LED
int state = LOW;

// Ein Metro-Objekt, das alle 1000 Millisekunden tickt
Metro ledMetro(1000);


void setup()
{
    pinMode(LEDPin, OUTPUT);
}


void loop()
{
    // Wechsle bei jedem Tick des LED-Metro zwischen LOW und HIGH
    if (ledMetro.check()) {
        state = (HIGH - state);
        digitalWrite(LEDPin, state);
    }
}
