# Fritzing sketch LEDBalken (saved by Fritzing 0.9.2b)
breadboards: 1

parts:
  Bauteil1 = Arduino Uno (Rev3)
  R1 = Resistor [tolerance=±5% resistance=1k package=THT]
  R2 = Resistor [tolerance=±5% resistance=1k package=THT]
  R3 = Resistor [tolerance=±5% resistance=1k package=THT]
  R4 = Resistor [tolerance=±5% resistance=1k package=THT]
  R5 = Resistor [tolerance=±5% resistance=1k package=THT]
  R6 = Resistor [tolerance=±5% resistance=1k package=THT]
  R7 = Resistor [tolerance=±5% resistance=1k package=THT]
  R8 = Resistor [tolerance=±5% resistance=1k package=THT]
  R9 = Resistor [tolerance=±5% resistance=1k package=THT]
  R10 = Resistor [tolerance=±5% resistance=1k package=THT]
  D1 = LED_BARGRAPH_10 [package=led_bargaph_10]
  R11 = TRIMPOT [package=3362u-2]

nets:
  N1: Bauteil1.A0, R11.WIPER
  N2: Bauteil1.D8, D1.E_A
  N3: Bauteil1.D9_PWM, D1.D_A
  N4: Bauteil1.D10_PWM/SS, D1.C_A
  N5: Bauteil1.D11_PWM/MOSI, D1.B_A
  N6: Bauteil1.D12/MISO, D1.A_A
  N7: Bauteil1.GND, R1.Pin_0, R2.Pin_0, R3.Pin_0, R4.Pin_0, R5.Pin_0, R6.Pin_0, R7.Pin_0, R8.Pin_0, R9.Pin_0, R10.Pin_0, R11.CCW
  N8: Bauteil1.D3_PWM, D1.J_A
  N9: Bauteil1.D4, D1.I_A
  N10: Bauteil1.D5_PWM, D1.H_A
  N11: Bauteil1.D6_PWM, D1.G_A
  N12: Bauteil1.D7, D1.F_A
  N13: Bauteil1.5V, R11.CW
  N14: R1.Pin_1, D1.A_C
  N15: R2.Pin_1, D1.B_C
  N16: R3.Pin_1, D1.C_C
  N17: R4.Pin_1, D1.D_C
  N18: R5.Pin_1, D1.E_C
  N19: R6.Pin_1, D1.F_C
  N20: R7.Pin_1, D1.G_C
  N21: R8.Pin_1, D1.H_C
  N22: R9.Pin_1, D1.I_C
  N23: R10.Pin_1, D1.J_C
