# Fritzing sketch Lichtfalle (saved by Fritzing 0.9.1b)
breadboards: 1

parts:
  Bauteil1 = Arduino Uno (Rev3)
  J1 = Piezo Speaker
  Q1 = LTR-301 [package=ltr-301]
  R2 = Resistor [tolerance=±5% resistance=10k package=THT]
  D1 = LTE-302 [package=lte-302]
  R1 = Resistor [tolerance=±5% resistance=220 package=THT]
  R3 = Resistor [tolerance=±5% resistance=220 package=THT]

nets:
  N1: Bauteil1.D12/MISO, R1.Pin_1
  N2: Bauteil1.D2, Q1.E, R2.Pin_0
  N3: Bauteil1.5V, R2.Pin_1, R3.Pin_0
  N4: Bauteil1.GND, J1.pin1, Q1.C, D1.C
  N5: J1.pin2, R1.Pin_0
  N6: D1.A, R3.Pin_1

notes:
  IR-Sender: oben, gelber Punkt
  IR-Empfänger: unten, roter Punkt
