# Fritzing sketch RemoteControl (saved by Fritzing 0.9.2b)
breadboards: 1

parts:
  Bauteil1 = Arduino Uno (Rev3)
  LED1 = LEDs [package=led10mm]
  R1 = Resistor [tolerance=±5% resistance=100 package=THT]
  KEYPAD1 = Membrane Matrix Keypad

nets:
  N1: Bauteil1.D8, KEYPAD1.3
  N2: Bauteil1.D9_PWM, KEYPAD1.2
  N3: Bauteil1.D10_PWM/SS, KEYPAD1.1
  N4: Bauteil1.GND, R1.Pin_1
  N5: Bauteil1.D3_PWM, LED1.C
  N6: Bauteil1.D4, KEYPAD1.7
  N7: Bauteil1.D5_PWM, KEYPAD1.6
  N8: Bauteil1.D6_PWM, KEYPAD1.5
  N9: Bauteil1.D7, KEYPAD1.4
  N10: LED1.A, R1.Pin_0

custom parts:
  Membrane Matrix Keypad: Membrane Matrix 3x4 Keypad
