# Fritzing sketch RemoteLEDShow (saved by Fritzing 0.9.2b)
breadboards: 1

parts:
  Bauteil1 = Arduino Uno (Rev3)
  R1 = Resistor [tolerance=±5% resistance=1k package=THT]
  R2 = Resistor [tolerance=±5% resistance=1k package=THT]
  R3 = Resistor [tolerance=±5% resistance=1k package=THT]
  R4 = Resistor [tolerance=±5% resistance=1k package=THT]
  R5 = Resistor [tolerance=±5% resistance=1k package=THT]
  R6 = Resistor [tolerance=±5% resistance=1k package=THT]
  R7 = Resistor [tolerance=±5% resistance=1k package=THT]
  R8 = Resistor [tolerance=±5% resistance=1k package=THT]
  R9 = Resistor [tolerance=±5% resistance=1k package=THT]
  R10 = Resistor [tolerance=±5% resistance=1k package=THT]
  D1 = LED_BARGRAPH_10 [package=led_bargaph_10]
  IR1 = TSOP312.., 314.. [package=THT]  # not connected

nets:
  N1: Bauteil1.D8, D1.E_A
  N2: Bauteil1.D9_PWM, D1.D_A
  N3: Bauteil1.D10_PWM/SS, D1.C_A
  N4: Bauteil1.D11_PWM/MOSI, D1.B_A
  N5: Bauteil1.D12/MISO, D1.A_A
  N6: Bauteil1.GND, R1.Pin_0, R2.Pin_0, R3.Pin_0, R4.Pin_0, R5.Pin_0, R6.Pin_0, R7.Pin_0, R8.Pin_0, R9.Pin_0, R10.Pin_0
  N7: Bauteil1.D3_PWM, D1.J_A
  N8: Bauteil1.D4, D1.I_A
  N9: Bauteil1.D5_PWM, D1.H_A
  N10: Bauteil1.D6_PWM, D1.G_A
  N11: Bauteil1.D7, D1.F_A
  N12: R1.Pin_1, D1.A_C
  N13: R2.Pin_1, D1.B_C
  N14: R3.Pin_1, D1.C_C
  N15: R4.Pin_1, D1.D_C
  N16: R5.Pin_1, D1.E_C
  N17: R6.Pin_1, D1.F_C
  N18: R7.Pin_1, D1.G_C
  N19: R8.Pin_1, D1.H_C
  N20: R9.Pin_1, D1.I_C
  N21: R10.Pin_1, D1.J_C

notes:
  Anschlüsse von TSOP38238:
  OUT / GND / Vin (2.5 - 5.5 V)
