# Fritzing sketch SevenSegments (saved by Fritzing 0.9.2b)
breadboards: 1

parts:
  Bauteil1 = Arduino Uno (Rev3)
  LED1 = 7-SEGMENT-4DIGIT-YOUNGSUN [package=7-segment-4digit-youngsun]
  R1 = Resistor [tolerance=±5% resistance=1k package=THT]
  R2 = Resistor [tolerance=±5% resistance=1k package=THT]
  R3 = Resistor [tolerance=±5% resistance=1k package=THT]
  R4 = Resistor [tolerance=±5% resistance=1k package=THT]
  R5 = Resistor [tolerance=±5% resistance=1k package=THT]

nets:
  N1: Bauteil1.A0, LED1.DP
  N2: Bauteil1.A1, LED1.COL-A
  N3: Bauteil1.D8, LED1.G
  N4: Bauteil1.D9_PWM, R2.Pin_0
  N5: Bauteil1.D10_PWM/SS, R3.Pin_0
  N6: Bauteil1.D11_PWM/MOSI, R5.Pin_1
  N7: Bauteil1.D12/MISO, R4.Pin_1
  N8: Bauteil1.GND, R1.Pin_0
  N9: Bauteil1.D2, LED1.A
  N10: Bauteil1.D3_PWM, LED1.B
  N11: Bauteil1.D4, LED1.C
  N12: Bauteil1.D5_PWM, LED1.D
  N13: Bauteil1.D6_PWM, LED1.E
  N14: Bauteil1.D7, LED1.F
  N15: LED1.DIG1, R2.Pin_1
  N16: LED1.DIG2, R3.Pin_1
  N17: LED1.DIG3, R5.Pin_0
  N18: LED1.DIG4, R4.Pin_0
  N19: LED1.COL-C, R1.Pin_1
