# Fritzing sketch SoundMachine (saved by Fritzing 0.9.1b)
breadboards: 1

parts:
  Bauteil1 = Arduino Uno (Rev3)
  J1 = Piezo Speaker
  R1 = Resistor [tolerance=±5% resistance=220 package=THT]

nets:
  N1: Bauteil1.D12/MISO, R1.Pin_1
  N2: Bauteil1.GND, J1.pin1
  N3: J1.pin2, R1.Pin_0
