# Fritzing sketch Temperatur (saved by Fritzing 0.9.2b)
breadboards: 1

parts:
  Bauteil1 = Arduino Uno (Rev3)
  Bauteil2 = 7-Segment Serial Display (Sparkfun COM-1144x, COM-11629) [part_number=COM-1144x]  # not connected
  R1 = Resistor [tolerance=±5% resistance=4.7k package=THT]

nets:
  N1: Bauteil1.D2, R1.Pin_0
  N2: Bauteil1.5V, R1.Pin_1

notes:
  Temperatursensor
  wasserdicht
  mit DS18B20

custom parts:
  7-Segment Serial Display (Sparkfun COM-1144x, COM-11629): Description: The 7-Segment Serial Display combines a classic 4-digit 7-segment display and an ATMega328 microcontroller allowing you to control every segment individually using only a few serial lines. It can be controlled in one of three ways: Serial TTL communication, SPI serial communication or I2C serial. You can even program it for stand-alone operation since the ATMega328 comes pre-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
